// Logisim project TP2.circ as structural Verilog: 8 circuits, main circuit main
module main (
);


  // Notes on the sheet:
  //   1.1
  //   HAROUNE Neyla
  //   RIGNAULT TOUZET Alice
endmodule

module CPT6Binary (
  input  [5:0] D,
  input  load,
  input  inc,
  input  clk,
  input  rst,
  output [5:0] Q
);

  wire or_1_out;
  wire [5:0] adder_1_out, multiplexer_1_out;

  Adder #(.width(6)) adder_1 (.a(Q), .b(6'b000001), .out(adder_1_out), .cin(1'b0));  // open: cout
  Multiplexer #(.width(6), .enable("false")) multiplexer_1 (
    .in0(adder_1_out), .in1(D), .out(multiplexer_1_out), .sel(load));
  or or_1 (or_1_out, load, inc);
  Register #(.width(6)) register_1 (.D(multiplexer_1_out), .en(or_1_out), .clk(clk), .Q(Q), .clr(rst));
endmodule

module test_CPT6Binary (
  input  load,
  input  inc,
  input  rst
);

  wire clk_out;
  wire [5:0] cpt6binary_1_q, dipswitch_1_sw6;

  Clock sysclk ();  // open: out
  Clock clk (.out(clk_out));
  DipSwitch #(.number(6)) dipswitch_1 (
    .sw1(dipswitch_1_sw6[5]), .sw2(dipswitch_1_sw6[4]), .sw3(dipswitch_1_sw6[3]), .sw4(dipswitch_1_sw6[2]),
    .sw5(dipswitch_1_sw6[1]), .sw6(dipswitch_1_sw6[0]));
  CPT6Binary cpt6binary_1 (.D(dipswitch_1_sw6), .load(load), .inc(inc), .clk(clk_out), .rst(rst), .Q(cpt6binary_1_q));
  LED LED0 (.in(cpt6binary_1_q[0]));
  LED LED1 (.in(cpt6binary_1_q[1]));
  LED LED2 (.in(cpt6binary_1_q[2]));
  LED LED3 (.in(cpt6binary_1_q[3]));
  LED LED4 (.in(cpt6binary_1_q[4]));
  LED LED5 (.in(cpt6binary_1_q[5]));

  // Notes on the sheet:
  //   Test du compteur à 6 bits en entrée
endmodule

module CPT6BinaryModP (
  input  [5:0] P,
  input  inc,
  input  clk,
  input  rst,
  output Tic,
  output [5:0] Q
);

  wire comparator_1_eq;

  Comparator #(.width(6), .mode("unsigned")) comparator_1 (.a(Q), .b(P), .eq(comparator_1_eq));  // open: gt, lt
  and and_1 (Tic, comparator_1_eq, inc);
  CPT6Binary cpt6binary_1 (.D({6{1'b0}}), .load(Tic), .inc(inc), .clk(clk), .rst(rst), .Q(Q));
endmodule

module test_CPT6BinaryModP (
  input  inc,
  input  rst,
  output Tic,
  output [5:0] Q
);

  wire clk_out;

  Clock sysclk ();  // open: out
  Clock clk (.out(clk_out));
  CPT6BinaryModP cpt6binarymodp_1 (.P({6{1'b0}}), .inc(inc), .clk(clk_out), .rst(rst), .Tic(Tic), .Q(Q));

  // Notes on the sheet:
  //   Test du compteur modulo P à 6 bits en entrée
endmodule

module test_CPT6BinaryModPHexa (
  input  [5:0] P,
  input  inc,
  input  rest,
  output Tic
);

  wire clk_out;
  wire [5:0] cpt6binarymodp_1_q;

  Clock clk (.out(clk_out));
  CPT6BinaryModP cpt6binarymodp_1 (.P(P), .inc(inc), .clk(clk_out), .rst(rest), .Tic(Tic), .Q(cpt6binarymodp_1_q));
  Hex_Digit_Display hex_digit_display_1 (.value({2'b00, cpt6binarymodp_1_q[5:4]}));  // open: dp
  Hex_Digit_Display hex_digit_display_2 (.value(cpt6binarymodp_1_q[3:0]));  // open: dp

  // Notes on the sheet:
  //   Test du compteur 6 bits modulo P avec affichage hexadécimal
  //   Affichage
  //   poids forts
  //   poids faibles
endmodule

module Watch (
  input  in_1,
  input  in_2,
  input  in_3,
  input  rst
);

  wire clk_out, cpt6binarymodp_2_tic, cpt6binarymodp_3_tic, H1_p1, H1_p2, M1_p1, M1_p2, S1_p1, S1_p2;
  wire [5:0] cpt6binarymodp_1_q, cpt6binarymodp_2_q, cpt6binarymodp_3_q;

  Clock clk (.out(clk_out));
  CPT6BinaryModP cpt6binarymodp_1 (
    .P(6'b011000), .inc(in_1), .clk(cpt6binarymodp_2_tic), .rst(rst), .Q(cpt6binarymodp_1_q));  // open: Tic
  CPT6BinaryModP cpt6binarymodp_2 (
    .P(6'b111100), .inc(in_2), .clk(cpt6binarymodp_3_tic), .rst(rst), .Tic(cpt6binarymodp_2_tic),
    .Q(cpt6binarymodp_2_q));
  // _7_Segment_Display H1: pin names not known; wires that end beside it: H1_p1, H1_p2
  // BCD_to_7_Segment_decoder bcd_to_7_segment_decoder_1: pin names not known
  // BCD_to_7_Segment_decoder bcd_to_7_segment_decoder_2: pin names not known
  _7_Segment_Display H0 ();  // open: g, f, a, b, e, d, c, dp
  // Binary_to_BCD_converter #(.binvalue(6)) binary_to_bcd_converter_1: pin names not known; wires that end beside it: cpt6binarymodp_1_q, H1_p1, H1_p2
  // _7_Segment_Display M1: pin names not known; wires that end beside it: M1_p1, M1_p2
  // BCD_to_7_Segment_decoder bcd_to_7_segment_decoder_3: pin names not known
  // Binary_to_BCD_converter #(.binvalue(6)) binary_to_bcd_converter_2: pin names not known; wires that end beside it: cpt6binarymodp_2_q, M1_p1, M1_p2
  CPT6BinaryModP cpt6binarymodp_3 (
    .P(6'b111100), .inc(in_3), .clk(clk_out), .rst(rst), .Tic(cpt6binarymodp_3_tic), .Q(cpt6binarymodp_3_q));
  _7_Segment_Display M0 ();  // open: g, f, a, b, e, d, c, dp
  // BCD_to_7_Segment_decoder bcd_to_7_segment_decoder_4: pin names not known
  // _7_Segment_Display S1: pin names not known; wires that end beside it: S1_p1, S1_p2
  // BCD_to_7_Segment_decoder bcd_to_7_segment_decoder_5: pin names not known
  _7_Segment_Display S0 ();  // open: g, f, a, b, e, d, c, dp
  // BCD_to_7_Segment_decoder bcd_to_7_segment_decoder_6: pin names not known
  // Binary_to_BCD_converter #(.binvalue(6)) binary_to_bcd_converter_3: pin names not known; wires that end beside it: cpt6binarymodp_3_q, S1_p1, S1_p2

  // Notes on the sheet:
  //   TP2 montre numérique 
  //   Heure
  //   Minute
  //   Seconde
endmodule

module AvecReveil (
  input  rst,
  input  [5:0] ValReveil,
  input  majH,
  input  majM,
  input  Sonnerie
);

  Clock clk ();  // open: out
  CPT6BinaryModP cpt6binarymodp_1 ();  // open: P, inc, clk, rst, Tic, Q
  CPT6BinaryModP cpt6binarymodp_2 ();  // open: P, inc, clk, rst, Tic, Q
  // BCD_to_7_Segment_decoder bcd_to_7_segment_decoder_1: pin names not known
  _7_Segment_Display u_7_segment_display_1 ();  // open: g, f, a, b, e, d, c, dp
  _7_Segment_Display u_7_segment_display_2 ();  // open: g, f, a, b, e, d, c, dp
  // BCD_to_7_Segment_decoder bcd_to_7_segment_decoder_2: pin names not known
  CPT6BinaryModP cpt6binarymodp_3 ();  // open: P, inc, clk, rst, Tic, Q
  _7_Segment_Display u_7_segment_display_3 ();  // open: g, f, a, b, e, d, c, dp
  // BCD_to_7_Segment_decoder bcd_to_7_segment_decoder_3: pin names not known
  // BCD_to_7_Segment_decoder bcd_to_7_segment_decoder_4: pin names not known
  _7_Segment_Display u_7_segment_display_4 ();  // open: g, f, a, b, e, d, c, dp
  _7_Segment_Display u_7_segment_display_5 ();  // open: g, f, a, b, e, d, c, dp
  _7_Segment_Display u_7_segment_display_6 ();  // open: g, f, a, b, e, d, c, dp
  // BCD_to_7_Segment_decoder bcd_to_7_segment_decoder_5: pin names not known
  // BCD_to_7_Segment_decoder bcd_to_7_segment_decoder_6: pin names not known
  LED BIP ();  // open: in

  // Notes on the sheet:
  //   TP2 montre numérique avec réveil
  //   Heure
  //   Minute
  //   Seconde
endmodule
