// Logisim project TP3_HAROUNE_RIGNAULT TOUZET_1.1.circ as structural Verilog: 4 circuits, main circuit SREG8
module chenillard_fsm (
  input  rst
);

  wire clk_out;
  wire [7:0] fsm_entity_1_p5;

  Clock clk (.out(clk_out));
  // FSM_Entity #(.content("state_machine example @[50,50,800,500]{\n	in NOP[1]   @[50,100,31,15];\n	out L[8]   @[813,140,37,15];\n	codeWidth = 4;\n	reset = S0;\n	\n	state S0[\"0000\"]:\n	 	@[84,112,30,30]\n		set L=\"00000001\";  @[84,112,30,30]	\n		goto S1  when default   @[253,96,45,23]; \n	state S1[\"0001\"]:\n	 	@[375,89,30,30]\n		set L=\"00000010\";  @[375,89,30,30]	\n		goto S2  when default   @[501,87,45,23]; \n	state S2[\"0010\"]:\n	 	@[594,83,30,30]\n		set L=\"00000100\";  @[594,83,30,30]	\n		goto S3  when default   @[733,144,45,23]; \n	state S3[\"0011\"]:\n	 	@[739,254,30,30]\n		set L=\"00001000\";  @[739,254,30,30]	\n		goto S4  when default   @[756,411,45,23]; \n	state S4[\"0100\"]:\n	 	@[615,483,30,30]\n		set L=\"00010000\";  @[615,483,30,30]	\n		goto S5  when default   @[531,519,45,23]; \n	state S5[\"0101\"]:\n	 	@[349,478,30,30]\n		set L=\"00100000\";  @[349,478,30,30]	\n		goto S6  when default   @[228,507,45,23]; \n	state S6[\"0110\"]:\n	 	@[129,449,30,30]\n		set L=\"01000000\";  @[129,449,30,30]	\n		goto S7  when default   @[78,415,45,23]; \n	state S7[\"0111\"]:\n	 	@[37,284,30,30]\n		set L=\"10000000\";  @[37,284,30,30]	\n		goto S8  when default   @[125,331,45,23]; \n	state S8[\"1000\"]:\n	 	@[178,387,30,30]\n		set L=\"01000000\";  @[178,387,30,30]	\n		goto S9  when default   @[278,368,45,23]; \n	state S9[\"1001\"]:\n	 	@[361,406,30,30]\n		set L=\"00100000\";  @[361,406,30,30]	\n		goto S10  when default   @[482,394,45,23]; \n	state S10[\"1010\"]:\n	 	@[595,408,30,30]\n		set L=\"00010000\";  @[595,408,30,30]	\n		goto S11  when default   @[606,364,45,23]; \n	state S11[\"1011\"]:\n	 	@[640,268,30,30]\n		set L=\"00001000\";  @[640,268,30,30]	\n		goto S12  when default   @[624,270,45,23]; \n	state S12[\"1100\"]:\n	 	@[549,156,30,30]\n		set L=\"00000100\";  @[549,156,30,30]	\n		goto S13  when default   @[474,182,45,23]; \n	state S13[\"1101\"]:\n	 	@[312,167,30,30]\n		set L=\"00000010\";  @[312,167,30,30]	\n		goto S0  when default   @[241,165,45,23]; \n}")) fsm_entity_1: pin names not known; wires that end beside it: clk_out, rst, 1'b1, 1'b1, fsm_entity_1_p5
  LED LED0 (.in(fsm_entity_1_p5[0]));
  LED LED1 (.in(fsm_entity_1_p5[1]));
  LED LED2 (.in(fsm_entity_1_p5[2]));
  LED LED3 (.in(fsm_entity_1_p5[3]));
  LED LED4 (.in(fsm_entity_1_p5[4]));
  LED LED5 (.in(fsm_entity_1_p5[5]));
  LED LED6 (.in(fsm_entity_1_p5[6]));
  LED LED7 (.in(fsm_entity_1_p5[7]));
endmodule

module SREG8 (
  input  clk,
  input  rst,
  input  sin,
  input  [1:0] C,
  input  [7:0] D,
  output sout,
  output [7:0] Q
);

  wire xor_1_out;
  wire [7:0] multiplexer_1_out;

  Multiplexer #(.width(8), .enable("false")) multiplexer_1 (
    .in0({sin, Q[7:1]}), .in1(D), .out(multiplexer_1_out), .sel(C[0]));
  Register register_1 (.D(multiplexer_1_out), .en(xor_1_out), .clk(clk), .Q(Q), .clr(rst));
  xor xor_1 (xor_1_out, C[0], C[1]);

  assign sout = Q[0];
endmodule

module parity (
  input  [7:0] din,
  output parity
);

  wire xor_1_out, xor_2_out, xor_3_out, xor_4_out, xor_5_out, xor_6_out;

  xor xor_1 (xor_1_out, din[0], din[1]);
  xor xor_2 (xor_2_out, din[2], din[3]);
  xor xor_3 (xor_3_out, din[4], din[5]);
  xor xor_4 (xor_4_out, din[6], din[7]);
  xor xor_5 (xor_5_out, xor_1_out, xor_2_out);
  xor xor_6 (xor_6_out, xor_3_out, xor_4_out);
  xor xor_7 (parity, xor_5_out, xor_6_out);
endmodule

module TP3_student (
  input  rst,
  output ERR
);

  wire clk, fsm_entity_1_p6, fsm_entity_1_p8, mysterymessage_1_p3, parity_1_parity;
  wire [1:0] fsm_entity_1_p7;
  wire [7:0] sreg8_1_q;

  Clock sysclk (.out(clk));
  // MysteryMessage mysterymessage_1: pin names not known; wires that end beside it: clk, rst, mysterymessage_1_p3
  // FSM_Entity #(.content("state_machine example @[80,61,800,500]{\n	in NOP[1]   @[80,100,31,15];rx[1]   @[80,248,17,15];ack[1]   @[80,338,25,15];\n	out C[2]   @[841,214,39,15];req[1]   @[855,307,25,15];error[1]   @[845,405,35,15];\n	codeWidth = 4;\n	reset = S0;\n	\n	state S0[\"0000\"]:\n	 	@[118,171,30,30]\n		goto S1  when (/rx)   @[197,168,29,23]; \n	state S1[\"0001\"]:\n	 	@[246,141,30,30]\n		set C=\"10\";  @[246,141,30,30]	\n		goto S2  when default   @[318,157,45,23]; \n	state S2[\"0010\"]:\n	 	@[369,149,30,30]\n		set C=\"10\";  @[369,149,30,30]	\n		goto S3  when default   @[449,171,45,23]; \n	state S3[\"0011\"]:\n	 	@[504,151,30,30]\n		set C=\"10\";  @[504,151,30,30]	\n		goto S4  when default   @[578,192,45,23]; \n	state S4[\"0100\"]:\n	 	@[626,179,30,30]\n		set C=\"10\";  @[626,179,30,30]	\n		goto S5  when default   @[654,255,45,23]; \n	state S5[\"0101\"]:\n	 	@[671,264,30,30]\n		set C=\"10\";  @[671,264,30,30]	\n		goto S6  when default   @[655,326,45,23]; \n	state S6[\"0110\"]:\n	 	@[609,354,30,30]\n		set C=\"10\";  @[609,354,30,30]	\n		goto S7  when default   @[570,380,45,23]; \n	state S7[\"0111\"]:\n	 	@[509,378,30,30]\n		set C=\"10\";  @[509,378,30,30]	\n		goto S8  when default   @[445,401,45,23]; \n	state S8[\"1000\"]:\n	 	@[344,388,30,30]\n		set C=\"10\";  @[344,388,30,30]	\n		goto S9  when default   @[275,393,45,23]; \n	state S9[\"1001\"]:\n	 	@[241,360,30,30]\n		set C=\"11\";req=\"1\";  @[241,360,30,30]	\n		goto S10  when ack   @[224,346,25,23]; \n	state S10[\"1010\"]:\n	 	@[170,277,30,30]\n		set req=\"0\";  @[170,277,30,30]	\n		goto S0  when (/ack)   @[162,238,37,23]; \n}")) fsm_entity_1: pin names not known; wires that end beside it: clk, rst, 1'b1, 1'b1, mysterymessage_1_p3, fsm_entity_1_p6, fsm_entity_1_p7, fsm_entity_1_p8
  // Probe on sreg8_1_q
  SREG8 sreg8_1 (.clk(clk), .rst(rst), .sin(mysterymessage_1_p3), .C(fsm_entity_1_p7), .Q(sreg8_1_q));  // open: D, sout
  parity parity_1 (.din(sreg8_1_q), .parity(parity_1_parity));
  // TTYPFO #(.cols(40)) ttypfo_1: pin names not known; wires that end beside it: clk, fsm_entity_1_p8, fsm_entity_1_p6, sreg8_1_q, rst
  xor xor_1 (ERR, mysterymessage_1_p3, parity_1_parity);

  // Notes on the sheet:
  //   Simulation de l'emetteur
  //   TX
  //   REQ
  //   ACK
  //   DATA
  //   Afficheur de caractères (code ASCII)
endmodule
