// Logisim project Div8x8.circ as structural Verilog: 1 circuit, main circuit main
module main (
  input  [7:0] D,
  input  rst,
  input  Req,
  output Ack,
  output [7:0] Res
);

  wire AinfB, clk, selA, selK, wA, wB, wK;
  wire [7:0] A, adder_1_out, B_q, multiplexer_1_out, multiplexer_2_out, subtractor_1_out;

  Clock u_clk (.out(clk));
  // FSM_Entity #(.content("state_machine example @[50,50,800,500]{\n	in AinfB[1]   @[50,100,36,15];Req[1]   @[50,145,27,15];\n	out wA[1]   @[827,140,23,15];selA[1]   @[820,164,30,15];wB[1]   @[827,189,23,15];wK[1]   @[828,213,22,15];ACK[1]   @[821,264,29,15];selK[1]   @[821,290,29,15];\n	codeWidth = 4;\n	reset = S0;\n	\n	state S0[\"0000\"]:\n	 	@[332,105,30,30]\n		set wA=\"1\";  @[332,105,30,30]	\n		goto S1  when Req   @[258,148,27,23]; \n	state S1[\"0001\"]:\n	 	@[159,174,30,30]\n		set ACK=\"1\";  @[159,174,30,30]	\n		goto S2  when (/Req)   @[145,244,39,23]; \n	state S2[\"0010\"]:\n	 	@[79,270,30,30]\n		set wB=\"1\";wK=\"1\";  @[79,270,30,30]	\n		goto S4  when Req   @[106,347,27,23]; \n	state suiv[\"0101\"]:\n	 	@[446,332,30,30]\n		set ACK=\"1\";  @[446,332,30,30]	\n		goto S0  when (/Req)   @[448,202,39,23]; \n	state S4[\"0011\"]:\n	 	@[83,397,30,30]\n		goto S5  when (/AinfB)   @[217,477,48,23]; \n		goto suiv  when AinfB   @[263,370,36,23]; \n	state S5[\"0100\"]:\n	 	@[365,451,30,30]\n		set wA=\"1\";selA=\"1\";wK=\"1\";selK=\"1\";  @[365,451,30,30]	\n		goto S4  when default   @[214,431,45,23]; \n}")) fsm_entity_1: pin names not known; wires that end beside it: clk, rst, 1'b1, AinfB, Req, wA, selA, wB, wK, Ack, selK
  Multiplexer #(.width(8), .enable("false")) multiplexer_1 (
    .in0({8{1'b0}}), .in1(adder_1_out), .out(multiplexer_1_out), .sel(selK));
  Multiplexer #(.width(8), .enable("false")) multiplexer_2 (
    .in0(D), .in1(subtractor_1_out), .out(multiplexer_2_out), .sel(selA));
  Register B (.D(D), .en(wB), .clk(clk), .Q(B_q), .clr(rst));
  Register K (.D(multiplexer_1_out), .en(wK), .clk(clk), .Q(Res), .clr(rst));
  Register u_A (.D(multiplexer_2_out), .en(wA), .clk(clk), .Q(A), .clr(rst));
  Adder adder_1 (.a(Res), .b(8'h1), .out(adder_1_out));  // open: cin, cout
  Subtractor subtractor_1 (.a(A), .b(B_q), .out(subtractor_1_out));  // open: bin, bout
  Comparator comparator_1 (.a(A), .b(B_q), .lt(AinfB));  // open: gt, eq
endmodule
