// Logisim project Mul8x8.circ as structural Verilog: 1 circuit, main circuit Multiplieur8x8
module Multiplieur8x8 (
  input  rst,
  input  [7:0] E,
  input  REQ,
  output ACK,
  output [15:0] RES
);

  wire B0, clk, selA, selAcc, selB, selI, weA, weAcc, weB, weI;
  wire [2:0] adder_1_out, I, multiplexer_3_out;
  wire [7:0] DD, multiplexer_2_out;
  wire [7:1] mB_q;
  wire [15:0] adder_2_out, mA_q, multiplexer_1_out, multiplexer_4_out, shifter_1_out;

  Clock u_Clk (.out(clk));
  // FSM_Entity #(.content("state_machine UC_MUL @[98,44,800,500]{\n	in REQ[1]   @[98,133,29,15];B0[1]   @[98,271,21,15];I[3]   @[98,309,35,15];\n	out ACK[1]   @[869,85,29,15];selA[1]   @[868,127,30,15];weA[1]   @[868,146,30,15];selB[1]   @[868,178,30,15];weB[1]   @[868,199,30,15];selI[1]   @[872,244,26,15];weI[1]   @[872,267,26,15];selAcc[1]   @[856,360,42,15];weAcc[1]   @[856,380,42,15];\n	codeWidth = 4;\n	reset = IDLE;\n	\n	state IDLE[\"0000\"]:\n	 	@[136,87,30,30]\n		set selA=\"1\";weA=\"1\";  @[136,87,30,30]	\n		goto S1  when REQ   @[209,164,29,23]; \n	state S1[\"0001\"]:\n	 	@[245,202,30,30]\n		set ACK=\"1\";  @[245,202,30,30]	\n		goto S2  when (/REQ)   @[217,282,41,23]; \n	state S2[\"0010\"]:\n	 	@[162,327,30,30]\n		set selB=\"1\";weB=\"1\";weAcc=\"1\";  @[162,327,30,30]	\n		goto S3  when REQ   @[276,389,29,23]; \n	state S3[\"0011\"]:\n	 	@[300,448,30,30]\n		set weI=\"1\";selI=\"1\";  @[300,448,30,30]	\n		goto S4  when B0   @[459,477,21,23]; \n		goto S5  when (/B0)   @[512,328,33,23]; \n	state S4[\"0100\"]:\n	 	@[592,484,30,30]\n		set selAcc=\"1\";weAcc=\"1\";  @[592,484,30,30]	\n		goto S5  when default   @[662,431,45,23]; \n	state S5[\"0101\"]:\n	 	@[673,322,30,30]\n		set weA=\"1\";weB=\"1\";weI=\"1\";selI=\"1\";  @[673,322,30,30]	\n		goto S3  when (/(I==\"111\"))   @[528,412,75,23]; \n		goto S6  when (I==\"111\")   @[674,265,63,23]; \n	state S6[\"0110\"]:\n	 	@[649,145,30,30]\n		set ACK=\"1\";  @[649,145,30,30]	\n		goto IDLE  when (/REQ)   @[438,143,41,23]; \n}")) uc_mul_1: pin names not known; wires that end beside it: clk, rst, 1'b1, REQ, B0, I, ACK, selA, weA, selB, weB, selI, weI, selAcc, weAcc
  Multiplexer #(.width(16), .enable("false")) multiplexer_1 (
    .in0(shifter_1_out), .in1({{8{1'b0}}, E}), .out(multiplexer_1_out), .sel(selA));
  Multiplexer #(.width(8), .enable("false")) multiplexer_2 (.in0(DD), .in1(E), .out(multiplexer_2_out), .sel(selB));
  // Probe on multiplexer_1_out
  Multiplexer #(.width(3), .enable("false")) multiplexer_3 (
    .in0(3'b000), .in1(adder_1_out), .out(multiplexer_3_out), .sel(selI));
  Register #(.width(16)) mA (.D(multiplexer_1_out), .en(weA), .clk(clk), .Q(mA_q), .clr(rst));
  Register mB (.D(multiplexer_2_out), .en(weB), .clk(clk), .Q({mB_q, B0}), .clr(rst));
  Register #(.width(3)) u_i (.D(multiplexer_3_out), .en(weI), .clk(clk), .Q(I), .clr(rst));
  Adder #(.width(3)) adder_1 (.a(I), .b(3'b001), .out(adder_1_out));  // open: cin, cout
  Shifter #(.width(16)) shifter_1 (.in(mA_q), .\dist (4'b0001), .out(shifter_1_out));
  Shifter #(.shift("lr")) shifter_2 (.in({mB_q, B0}), .\dist (3'b001), .out(DD));
  Adder #(.width(16)) adder_2 (.a(mA_q), .b(RES), .out(adder_2_out));  // open: cin, cout
  Multiplexer #(.width(16), .enable("false")) multiplexer_4 (
    .in0({16{1'b0}}), .in1(adder_2_out), .out(multiplexer_4_out), .sel(selAcc));
  Register #(.width(16)) ACC (.D(multiplexer_4_out), .en(weAcc), .clk(clk), .Q(RES), .clr(rst));
endmodule
